# Fritzing sketch circuit (saved by Fritzing 0.9.3b)

parts:
  M1 = STM32F103C8T6 blue mini board
  BAT1 = Battery Holders [part_number=CR2032 package=battcom_20mm_pth]
  D1 = Schottky Diode [part_number=1N5817 package="300 mil [THT]"]
  LCD_1 = LCD 20x4 screen [part_number=20x4]
  R1 = Trimmer Potentiometer [maximum_resistance=10kΩ package=THT]

nets:
  N1: M1.B12, LCD_1.RS
  N2: M1.B13, LCD_1.R/W
  N3: M1.B14, LCD_1.E
  N4: M1.B15, LCD_1.DB4
  N5: M1.A8, LCD_1.DB5
  N6: M1.A9, LCD_1.DB6
  N7: M1.A10, LCD_1.DB7
  5V: M1.5V, LCD_1.VDD, LCD_1.LED+
  GND: M1.G, M1.GND, BAT1.-, LCD_1.VSS, LCD_1.LED-, R1.leg1, R1.wiper
  N8: M1.VBAT, D1.cathode
  N9: BAT1.+, D1.anode
  N10: LCD_1.V0, R1.leg2

custom parts:
  LCD 20x4 screen: A standard character display, usually with 2x16 characters. Comes in many colors.
