# Fritzing sketch circuit (saved by Fritzing 0.9.3b)

parts:
  M1 = STM32F103C8T6 blue mini board
  BAT1 = Battery Holders [package=battcom_20mm_pth]
  D1 = Schottky Diode [part_number=1N5817 package="300 mil [THT]"]

nets:
  N1: M1.VBAT, D1.cathode
  N2: M1.G, BAT1.-
  N3: BAT1.+, D1.anode
